// Logisim project circuitos.circ as structural Verilog: 4 circuits, main circuit main
module main (
  input  cin,
  input  [3:0] in_2,
  input  [3:0] in_3,
  output s0,
  output s1,
  output s2,
  output s3,
  output cout
);

  wire displaydecoder_1_p5, displaydecoder_1_p6, displaydecoder_1_p7, displaydecoder_1_p8,
       displaydecoder_1_p9, displaydecoder_1_p10, displaydecoder_1_p11, displaydecoder_2_p5,
       displaydecoder_2_p6, displaydecoder_2_p7, displaydecoder_2_p8, displaydecoder_2_p9,
       displaydecoder_2_p10, displaydecoder_2_p11, displaydecoder_3_p5, displaydecoder_3_p6,
       displaydecoder_3_p7, displaydecoder_3_p8, displaydecoder_3_p9, displaydecoder_3_p10,
       displaydecoder_3_p11;

  // DisplayDecoder #(.multibit("false")) displaydecoder_1: pin names not known; wires that end beside it: in_2[0], in_2[1], in_2[2], in_2[3], displaydecoder_1_p5, displaydecoder_1_p6, displaydecoder_1_p7, displaydecoder_1_p8, displaydecoder_1_p9, displaydecoder_1_p10, displaydecoder_1_p11
  _7_Segment_Display u_7_segment_display_1 (
    .g(displaydecoder_1_p11), .f(displaydecoder_1_p10), .a(displaydecoder_1_p5), .b(displaydecoder_1_p6),
    .e(displaydecoder_1_p9), .d(displaydecoder_1_p8), .c(displaydecoder_1_p7));  // open: dp
  _4bit_adder u_4bit_adder_1 (
    .in_2(in_2[0]), .in_3(in_2[1]), .in_4(in_2[2]), .in_5(in_2[3]), .in_6(in_3[0]), .in_7(in_3[1]),
    .in_8(in_3[2]), .in_9(in_3[3]), .cin(cin), .cout(cout), .s0(s0), .s1(s1), .s2(s2), .s3(s3));
  // DisplayDecoder #(.multibit("false")) displaydecoder_2: pin names not known; wires that end beside it: in_3[0], in_3[1], in_3[2], in_3[3], displaydecoder_2_p5, displaydecoder_2_p6, displaydecoder_2_p7, displaydecoder_2_p8, displaydecoder_2_p9, displaydecoder_2_p10, displaydecoder_2_p11
  _7_Segment_Display u_7_segment_display_2 (
    .g(displaydecoder_2_p11), .f(displaydecoder_2_p10), .a(displaydecoder_2_p5), .b(displaydecoder_2_p6),
    .e(displaydecoder_2_p9), .d(displaydecoder_2_p8), .c(displaydecoder_2_p7));  // open: dp
  // DisplayDecoder #(.multibit("false")) displaydecoder_3: pin names not known; wires that end beside it: s0, s1, s2, s3, displaydecoder_3_p5, displaydecoder_3_p6, displaydecoder_3_p7, displaydecoder_3_p8, displaydecoder_3_p9, displaydecoder_3_p10, displaydecoder_3_p11
  _7_Segment_Display u_7_segment_display_3 (
    .g(displaydecoder_3_p11), .f(displaydecoder_3_p10), .a(displaydecoder_3_p5), .b(displaydecoder_3_p6),
    .e(displaydecoder_3_p9), .d(displaydecoder_3_p8), .c(displaydecoder_3_p7));  // open: dp
endmodule

module half_adder (
  input  A,
  input  B,
  output sum,
  output cout
);

  xor xor_1 (sum, A, B);
  and and_1 (cout, A, B);
endmodule

module full_adder (
  input  C,
  input  A,
  input  B,
  output sum,
  output cout
);

  wire half_adder_1_cout, half_adder_1_sum, half_adder_2_cout;

  half_adder half_adder_1 (.A(A), .B(B), .sum(half_adder_1_sum), .cout(half_adder_1_cout));
  half_adder half_adder_2 (.A(half_adder_1_sum), .B(C), .sum(sum), .cout(half_adder_2_cout));
  or or_1 (cout, half_adder_2_cout, half_adder_1_cout);
endmodule

module _4bit_adder (
  input  cin,
  input  in_2,
  input  in_3,
  input  in_4,
  input  in_5,
  input  in_6,
  input  in_7,
  input  in_8,
  input  in_9,
  output s0,
  output s1,
  output s2,
  output s3,
  output cout
);

  wire full_adder_1_cout, full_adder_2_cout, full_adder_3_cout;

  full_adder full_adder_1 (.A(in_2), .B(in_6), .C(cin), .cout(full_adder_1_cout), .sum(s0));
  full_adder full_adder_2 (.A(in_3), .B(in_7), .C(full_adder_1_cout), .cout(full_adder_2_cout), .sum(s1));
  full_adder full_adder_3 (.A(in_4), .B(in_8), .C(full_adder_2_cout), .cout(full_adder_3_cout), .sum(s2));
  full_adder full_adder_4 (.A(in_5), .B(in_9), .C(full_adder_3_cout), .cout(cout), .sum(s3));
endmodule
