// Logisim project const.circ as structural Verilog: 9 circuits, main circuit Somador
module Somador (
  input  Ci,
  input  A0,
  input  B0,
  output S0,
  output Co
);

  wire and_1_out, and_2_out, xor_1_out;

  xor xor_1 (xor_1_out, A0, B0);
  and and_1 (and_1_out, B0, A0);
  xor xor_2 (S0, xor_1_out, Ci);
  and and_2 (and_2_out, xor_1_out, Ci);
  or or_1 (Co, and_2_out, and_1_out);
endmodule

module Soma_4bits (
  input  Ci,
  input  A0,
  input  B0,
  input  A1,
  input  B1,
  input  A2,
  input  B2,
  input  A3,
  input  B3,
  output S0,
  output S1,
  output S2,
  output S3,
  output overflow
);

  wire somador_1_co, somador_2_co, somador_3_co, somador_4_co;

  Somador somador_1 (.A0(A0), .B0(B0), .Ci(Ci), .S0(S0), .Co(somador_1_co));
  Somador somador_2 (.A0(A1), .B0(B1), .Ci(somador_1_co), .S0(S1), .Co(somador_2_co));
  Somador somador_3 (.A0(A2), .B0(B2), .Ci(somador_2_co), .S0(S2), .Co(somador_3_co));
  Somador somador_4 (.A0(A3), .B0(B3), .Ci(somador_3_co), .S0(S3), .Co(somador_4_co));
  xor xor_1 (overflow, somador_4_co, somador_3_co);
endmodule

module calculadora_4bits (
  input  in_1,
  input  in_2,
  input  in_3,
  input  in_4,
  input  in_5,
  input  in_6,
  input  in_7,
  input  in_8,
  input  in_9,
  output out_10,
  output out_11,
  output out_12,
  output out_13,
  output out_14
);

  wire decodificador_1_a, decodificador_1_b, decodificador_1_c, decodificador_1_d, decodificador_1_e,
       decodificador_1_f, decodificador_1_g, decodificador_1_h, decodificador_2_a, decodificador_2_b,
       decodificador_2_c, decodificador_2_d, decodificador_2_e, decodificador_2_f, decodificador_2_g,
       decodificador_2_h, decodificador_3_a, decodificador_3_b, decodificador_3_c, decodificador_3_d,
       decodificador_3_e, decodificador_3_f, decodificador_3_g, decodificador_3_h;

  Soma_4bits soma_4bits_1 (
    .Ci(in_1), .A0(in_2), .B0(in_6), .A1(in_3), .B1(in_7), .A2(in_4), .B2(in_8), .A3(in_5), .B3(in_9),
    .S0(out_10), .S1(out_11), .S2(out_12), .S3(out_13), .overflow(out_14));
  decodificador decodificador_1 (
    .S0(in_6), .S1(in_7), .S2(in_8), .S3(in_9), .a(decodificador_1_a), .b(decodificador_1_b),
    .c(decodificador_1_c), .d(decodificador_1_d), .e(decodificador_1_e), .f(decodificador_1_f),
    .g(decodificador_1_g), .h(decodificador_1_h));
  decodificador decodificador_2 (
    .S0(in_2), .S1(in_3), .S2(in_4), .S3(in_5), .a(decodificador_2_a), .b(decodificador_2_b),
    .c(decodificador_2_c), .d(decodificador_2_d), .e(decodificador_2_e), .f(decodificador_2_f),
    .g(decodificador_2_g), .h(decodificador_2_h));
  decodificador decodificador_3 (
    .S0(out_10), .S1(out_11), .S2(out_12), .S3(out_13), .a(decodificador_3_a), .b(decodificador_3_b),
    .c(decodificador_3_c), .d(decodificador_3_d), .e(decodificador_3_e), .f(decodificador_3_f),
    .g(decodificador_3_g), .h(decodificador_3_h));
  _7_Segment_Display u_7_segment_display_1 (
    .g(decodificador_1_a), .f(decodificador_1_b), .a(decodificador_1_c), .b(decodificador_1_d),
    .e(decodificador_1_e), .d(decodificador_1_f), .c(decodificador_1_g), .dp(decodificador_1_h));
  _7_Segment_Display u_7_segment_display_2 (
    .g(decodificador_2_a), .f(decodificador_2_b), .a(decodificador_2_c), .b(decodificador_2_d),
    .e(decodificador_2_e), .d(decodificador_2_f), .c(decodificador_2_g), .dp(decodificador_2_h));
  _7_Segment_Display u_7_segment_display_3 (
    .g(decodificador_3_a), .f(decodificador_3_b), .a(decodificador_3_c), .b(decodificador_3_d),
    .e(decodificador_3_e), .d(decodificador_3_f), .c(decodificador_3_g), .dp(decodificador_3_h));
endmodule

module decodificador (
  input  S0,
  input  S1,
  input  S2,
  input  S3,
  output a,
  output b,
  output c,
  output d,
  output e,
  output f,
  output g,
  output h
);

  wire and_1_out, and_2_out, and_3_out, and_4_out, and_5_out, and_6_out, and_7_out, and_8_out, and_9_out,
       and_10_out, and_11_out, and_12_out, and_13_out, and_14_out, and_15_out, and_16_out, and_17_out,
       and_18_out, and_19_out, and_20_out, and_21_out, and_22_out, and_23_out, and_24_out, and_25_out,
       and_26_out, and_27_out, and_28_out, and_29_out, and_30_out, and_31_out, and_32_out, and_33_out,
       and_34_out, and_35_out, and_36_out, not_1_out, not_2_out, not_3_out, not_4_out, not_5_out, not_6_out,
       not_7_out, not_8_out, not_9_out, not_10_out, not_11_out, not_12_out, not_13_out, not_14_out,
       not_15_out, not_16_out, not_17_out, not_18_out, not_19_out, not_20_out, not_21_out, not_22_out,
       not_23_out, not_24_out, not_25_out, not_26_out, not_27_out, not_28_out, not_29_out, not_30_out,
       not_31_out, not_32_out, not_33_out, not_34_out, not_35_out, not_36_out, not_37_out, not_38_out,
       not_39_out, not_40_out, not_41_out, not_42_out, not_43_out, not_44_out, not_45_out;

  not not_1 (not_1_out, S1);
  and and_1 (and_1_out, not_1_out, S2);
  and and_2 (and_2_out, S2, not_2_out);
  not not_2 (not_2_out, S3);
  not not_3 (not_3_out, S0);
  and and_3 (and_3_out, not_3_out, S1, not_4_out);
  not not_4 (not_4_out, S2);
  and and_4 (and_4_out, S0, not_5_out);
  not not_5 (not_5_out, S1);
  and and_5 (and_5_out, S0, S3);
  not not_6 (not_6_out, S2);
  and and_6 (and_6_out, not_6_out, not_7_out);
  not not_7 (not_7_out, S3);
  not not_8 (not_8_out, S0);
  and and_7 (and_7_out, not_8_out, S1, not_9_out);
  not not_9 (not_9_out, S2);
  and and_8 (and_8_out, S1, not_10_out);
  not not_10 (not_10_out, S3);
  and and_9 (and_9_out, S0, not_11_out);
  not not_11 (not_11_out, S1);
  and and_10 (and_10_out, S0, S2);
  not not_12 (not_12_out, S1);
  and and_11 (and_11_out, not_12_out, not_13_out);
  not not_13 (not_13_out, S3);
  not not_14 (not_14_out, S0);
  and and_12 (and_12_out, not_14_out, S2);
  not not_15 (not_15_out, S0);
  and and_13 (and_13_out, not_15_out, S1, S3);
  and and_14 (and_14_out, S1, S2);
  not not_16 (not_16_out, S1);
  and and_15 (and_15_out, S0, not_16_out, not_17_out);
  not not_17 (not_17_out, S2);
  and and_16 (and_16_out, S0, not_18_out);
  not not_18 (not_18_out, S3);
  not not_19 (not_19_out, S0);
  and and_17 (and_17_out, not_19_out, not_20_out);
  not not_20 (not_20_out, S1);
  not not_21 (not_21_out, S0);
  and and_18 (and_18_out, not_21_out, not_22_out, not_23_out);
  not not_22 (not_22_out, S2);
  not not_23 (not_23_out, S3);
  not not_24 (not_24_out, S1);
  and and_19 (and_19_out, not_24_out, not_25_out);
  not not_25 (not_25_out, S2);
  not not_26 (not_26_out, S1);
  and and_20 (and_20_out, not_26_out, not_27_out);
  not not_27 (not_27_out, S3);
  not not_28 (not_28_out, S0);
  and and_21 (and_21_out, not_28_out, S2, S3);
  and and_22 (and_22_out, S0, not_29_out, S3);
  not not_29 (not_29_out, S2);
  not not_30 (not_30_out, S1);
  and and_23 (and_23_out, not_30_out, not_31_out);
  not not_31 (not_31_out, S3);
  and and_24 (and_24_out, S2, not_32_out);
  not not_32 (not_32_out, S3);
  and and_25 (and_25_out, S0, S2);
  and and_26 (and_26_out, S0, S1);
  not not_33 (not_33_out, S0);
  and and_27 (and_27_out, not_33_out, not_34_out, not_35_out);
  not not_34 (not_34_out, S1);
  not not_35 (not_35_out, S3);
  not not_36 (not_36_out, S1);
  and and_28 (and_28_out, not_36_out, S2, S3);
  and and_29 (and_29_out, S1, not_37_out, S3);
  not not_37 (not_37_out, S2);
  and and_30 (and_30_out, S1, S2, not_38_out);
  not not_38 (not_38_out, S3);
  and and_31 (and_31_out, S0, not_39_out);
  not not_39 (not_39_out, S2);
  not not_40 (not_40_out, S0);
  and and_32 (and_32_out, not_40_out, not_41_out);
  not not_41 (not_41_out, S2);
  not not_42 (not_42_out, S0);
  and and_33 (and_33_out, not_42_out, S3);
  not not_43 (not_43_out, S2);
  and and_34 (and_34_out, not_43_out, S3);
  not not_44 (not_44_out, S0);
  and and_35 (and_35_out, not_44_out, S1);
  and and_36 (and_36_out, S0, not_45_out);
  not not_45 (not_45_out, S1);
  or or_1 (a, and_1_out, and_2_out, and_3_out, and_4_out, and_5_out);
  or or_2 (b, and_6_out, and_7_out, and_8_out, and_9_out, and_10_out);
  or or_3 (e, and_23_out, and_24_out, and_25_out, and_26_out);
  or or_4 (f, and_27_out, and_28_out, and_29_out, and_30_out, and_31_out);
  or or_5 (g, and_32_out, and_33_out, and_34_out, and_35_out, and_36_out);
  or or_6 (c, and_11_out, and_12_out, and_13_out, and_14_out, and_15_out, and_16_out);
  or or_7 (d, and_17_out, and_18_out, and_19_out, and_20_out, and_21_out, and_22_out);

  assign h = 1'b0;
endmodule

module teste (
  input  in_1,
  input  in_2,
  input  in_3,
  input  in_4,
  input  in_5,
  input  in_6,
  input  in_7,
  input  in_8,
  input  in_9,
  input  in_10,
  input  in_11,
  input  in_12
);

  wire decodificador_1_a, decodificador_1_b, decodificador_1_c, decodificador_1_d, decodificador_1_e,
       decodificador_1_f, decodificador_1_g, decodificador_1_h;

  _7_Segment_Display u_7_segment_display_1 (
    .g(in_5), .f(in_6), .a(in_7), .b(in_8), .e(in_9), .d(in_10), .c(in_11), .dp(in_12));
  decodificador decodificador_1 (
    .S0(in_1), .S1(in_2), .S2(in_3), .S3(in_4), .a(decodificador_1_a), .b(decodificador_1_b),
    .c(decodificador_1_c), .d(decodificador_1_d), .e(decodificador_1_e), .f(decodificador_1_f),
    .g(decodificador_1_g), .h(decodificador_1_h));
  _7_Segment_Display u_7_segment_display_2 (
    .g(decodificador_1_a), .f(decodificador_1_b), .a(decodificador_1_c), .b(decodificador_1_d),
    .e(decodificador_1_e), .d(decodificador_1_f), .c(decodificador_1_g), .dp(decodificador_1_h));
endmodule

module ALU (
  input  Binvert,
  input  Cin,
  input  op1,
  input  op2,
  input  A,
  input  B,
  output Result,
  output Cout
);

  wire and_1_out, binvert_1_out_4, not_1_out, not_2_out, or_1_out, somador_1_s0;

  not not_1 (not_1_out, B);
  Binvert binvert_1 (.A(B), .B(not_1_out), .porteiro(Binvert), .out_4(binvert_1_out_4));
  and and_1 (and_1_out, A, binvert_1_out_4);
  or or_1 (or_1_out, A, binvert_1_out_4);
  not not_2 (not_2_out, A);
  Somador somador_1 (.A0(A), .B0(binvert_1_out_4), .Ci(Cin), .S0(somador_1_s0), .Co(Cout));
  MUX mux_1 (.X(and_1_out), .Y(or_1_out), .Z(not_2_out), .W(somador_1_s0), .op1(op1), .op2(op2), .S(Result));
endmodule

module Binvert (
  input  porteiro,
  input  A,
  input  B,
  output out_4
);

  wire and_1_out, and_2_out, not_1_out;

  not not_1 (not_1_out, porteiro);
  and and_1 (and_1_out, A, not_1_out);
  and and_2 (and_2_out, B, porteiro);
  or or_1 (out_4, and_1_out, and_2_out);
endmodule

module MUX (
  input  op1,
  input  op2,
  input  X,
  input  Y,
  input  Z,
  input  W,
  output S
);

  wire and_1_out, and_2_out, and_3_out, and_4_out, not_1_out, not_2_out, not_3_out, not_4_out;

  not not_1 (not_1_out, op1);
  and and_1 (and_1_out, X, not_1_out, not_2_out);
  not not_2 (not_2_out, op2);
  not not_3 (not_3_out, op1);
  and and_2 (and_2_out, Y, not_3_out, op2);
  and and_3 (and_3_out, Z, op1, not_4_out);
  not not_4 (not_4_out, op2);
  and and_4 (and_4_out, W, op1, op2);
  or or_1 (S, and_1_out, and_2_out, and_3_out, and_4_out);
endmodule

module ULA_4bits (
  input  Binvert,
  input  op1,
  input  op2,
  input  B3,
  input  B2,
  input  B1,
  input  B0,
  input  A3,
  input  A2,
  input  A1,
  input  A0,
  output s0,
  output s1,
  output s2,
  output s3,
  output Cout
);

  wire alu_1_cout, alu_2_cout, alu_3_cout;

  ALU alu_1 (.A(A0), .B(B0), .Binvert(Binvert), .Cin(Binvert), .op1(op1), .op2(op2), .Result(s0), .Cout(alu_1_cout));
  ALU alu_2 (.A(A1), .B(B1), .Binvert(Binvert), .Cin(alu_1_cout), .op1(op1), .op2(op2), .Result(s1), .Cout(alu_2_cout));
  ALU alu_3 (.A(A2), .B(B2), .Binvert(Binvert), .Cin(alu_2_cout), .op1(op1), .op2(op2), .Result(s2), .Cout(alu_3_cout));
  ALU alu_4 (.A(A3), .B(B3), .Binvert(Binvert), .Cin(alu_3_cout), .op1(op1), .op2(op2), .Result(s3), .Cout(Cout));
endmodule
